// Logisim project 2bit_alu.circ as structural Verilog: 1 circuit, main circuit main
module main (
  input  A0,
  input  B0,
  input  CARRYIN,
  input  S0,
  input  S1,
  input  A1,
  input  B1,
  output OUT0,
  output OUT1,
  output CARRYOUT
);

  wire and_1_out, and_2_out, and_3_out, and_4_out, and_5_out, and_6_out, or_1_out, or_2_out, or_3_out,
       xor_1_out, xor_2_out, xor_3_out, xor_4_out, xor_5_out, xor_6_out;

  xor xor_1 (xor_1_out, A0, B0);
  and and_1 (and_1_out, A0, B0);
  or or_1 (or_1_out, A0, B0);
  xor xor_2 (xor_2_out, A0, B0);
  xor xor_3 (xor_3_out, A1, B1);
  and and_2 (and_2_out, A1, B1);
  or or_2 (or_2_out, A1, B1);
  xor xor_4 (xor_4_out, A1, B1);
  xor xor_5 (xor_5_out, xor_2_out, CARRYIN);
  and and_3 (and_3_out, CARRYIN, xor_2_out);
  and and_4 (and_4_out, B0, A0);
  xor xor_6 (xor_6_out, xor_4_out, or_3_out);
  and and_5 (and_5_out, or_3_out, xor_4_out);
  and and_6 (and_6_out, B1, A1);
  Multiplexer #(.select(2)) multiplexer_1 (
    .in0(xor_1_out), .in1(and_1_out), .in2(or_1_out), .in3(xor_5_out), .out(OUT0), .sel({S1, S0}));
  or or_3 (or_3_out, and_3_out, and_4_out);
  Multiplexer #(.select(2)) multiplexer_2 (
    .in0(xor_3_out), .in1(and_2_out), .in2(or_2_out), .in3(xor_6_out), .out(OUT1), .sel({S1, S0}));
  or or_4 (CARRYOUT, and_5_out, and_6_out);
endmodule
