// Logisim project 4bit_alu_shifter_wip.circ as structural Verilog: 1 circuit, main circuit main
module main (
  input  X1,
  input  X0,
  input  D3,
  input  D2,
  input  D1,
  input  D0,
  input  A0,
  input  B0,
  input  CARRYIN,
  input  S0,
  input  S1,
  input  A1,
  input  B1,
  input  A2,
  input  B2,
  input  A3,
  input  B3,
  output out_18,
  output out_19,
  output out_20,
  output out_21,
  output OUT0,
  output OUT1,
  output OUT2,
  output OUT3,
  output CARRYOUT
);

  wire and_1_out, and_2_out, and_3_out, and_4_out, and_5_out, and_6_out, and_7_out, and_8_out, and_9_out,
       and_10_out, and_11_out, and_12_out, CLK, d_ff_1_qn, d_ff_2_qn, d_ff_3_qn, d_ff_4_qn,
       multiplexer_1_out, multiplexer_2_out, multiplexer_3_out, multiplexer_4_out, or_1_out, or_2_out,
       or_3_out, or_4_out, or_5_out, or_6_out, or_7_out, xor_1_out, xor_2_out, xor_3_out, xor_4_out,
       xor_5_out, xor_6_out, xor_7_out, xor_8_out, xor_9_out, xor_10_out, xor_11_out, xor_12_out;

  Clock clock_1 (.out(CLK));
  xor xor_1 (xor_1_out, A0, B0);
  and and_1 (and_1_out, A0, B0);
  or or_1 (or_1_out, A0, B0);
  xor xor_2 (xor_2_out, A0, B0);
  xor xor_3 (xor_3_out, A1, B1);
  and and_2 (and_2_out, A1, B1);
  or or_2 (or_2_out, A1, B1);
  xor xor_4 (xor_4_out, A1, B1);
  xor xor_5 (xor_5_out, A2, B2);
  and and_3 (and_3_out, A2, B2);
  or or_3 (or_3_out, A2, B2);
  xor xor_6 (xor_6_out, A2, B2);
  xor xor_7 (xor_7_out, A3, B3);
  and and_4 (and_4_out, A3, B3);
  or or_4 (or_4_out, A3, B3);
  xor xor_8 (xor_8_out, A3, B3);
  Multiplexer #(.select(2)) multiplexer_1 (
    .in0(d_ff_1_qn), .in1(out_21), .in2(out_19), .in3(D0), .out(multiplexer_1_out), .sel({X1, X0}));
  Multiplexer #(.select(2)) multiplexer_2 (
    .in0(d_ff_2_qn), .in1(out_18), .in2(out_20), .in3(D1), .out(multiplexer_2_out), .sel({X1, X0}));
  Multiplexer #(.select(2)) multiplexer_3 (
    .in0(d_ff_3_qn), .in1(out_19), .in2(out_21), .in3(D2), .out(multiplexer_3_out), .sel({X1, X0}));
  Multiplexer #(.select(2)) multiplexer_4 (
    .in0(d_ff_4_qn), .in1(out_20), .in2(out_18), .in3(D3), .out(multiplexer_4_out), .sel({X1, X0}));
  xor xor_9 (xor_9_out, xor_2_out, CARRYIN);
  and and_5 (and_5_out, CARRYIN, xor_2_out);
  or or_5 (or_5_out, and_5_out, and_6_out);
  and and_6 (and_6_out, B0, A0);
  xor xor_10 (xor_10_out, xor_4_out, or_5_out);
  and and_7 (and_7_out, or_5_out, xor_4_out);
  or or_6 (or_6_out, and_7_out, and_8_out);
  and and_8 (and_8_out, B1, A1);
  xor xor_11 (xor_11_out, xor_6_out, or_6_out);
  and and_9 (and_9_out, or_6_out, xor_6_out);
  or or_7 (or_7_out, and_9_out, and_10_out);
  and and_10 (and_10_out, B2, A2);
  xor xor_12 (xor_12_out, xor_8_out, or_7_out);
  and and_11 (and_11_out, or_7_out, xor_8_out);
  or or_8 (CARRYOUT, and_11_out, and_12_out);
  and and_12 (and_12_out, B3, A3);
  D_Flip_Flop d_ff_1 (.D(multiplexer_1_out), .clk(CLK), .Q(out_18), .Qn(d_ff_1_qn));  // open: preset, reset
  D_Flip_Flop d_ff_2 (.D(multiplexer_2_out), .clk(CLK), .Q(out_19), .Qn(d_ff_2_qn));  // open: preset, reset
  D_Flip_Flop d_ff_3 (.D(multiplexer_3_out), .clk(CLK), .Q(out_20), .Qn(d_ff_3_qn));  // open: preset, reset
  D_Flip_Flop d_ff_4 (.D(multiplexer_4_out), .clk(CLK), .Q(out_21), .Qn(d_ff_4_qn));  // open: preset, reset
  Multiplexer #(.select(2)) multiplexer_5 (
    .in0(xor_1_out), .in1(and_1_out), .in2(or_1_out), .in3(xor_9_out), .out(OUT0), .sel({S1, S0}));
  Multiplexer #(.select(2)) multiplexer_6 (
    .in0(xor_3_out), .in1(and_2_out), .in2(or_2_out), .in3(xor_10_out), .out(OUT1), .sel({S1, S0}));
  Multiplexer #(.select(2)) multiplexer_7 (
    .in0(xor_5_out), .in1(and_3_out), .in2(or_3_out), .in3(xor_11_out), .out(OUT2), .sel({S1, S0}));
  Multiplexer #(.select(2)) multiplexer_8 (
    .in0(xor_7_out), .in1(and_4_out), .in2(or_4_out), .in3(xor_12_out), .out(OUT3), .sel({S1, S0}));

  // Other names for the same wires on the sheet: d = out_18; q = out_21
endmodule
