// Logisim project 4bit_shifter.circ as structural Verilog: 1 circuit, main circuit main
module main (
  input  X1,
  input  X0,
  input  D3,
  input  D2,
  input  D1,
  input  D0,
  output out_7,
  output out_8,
  output out_9,
  output out_10
);

  wire CLK, d_ff_1_qn, d_ff_2_qn, d_ff_3_qn, d_ff_4_qn, multiplexer_1_out, multiplexer_2_out,
       multiplexer_3_out, multiplexer_4_out;

  Clock clock_1 (.out(CLK));
  Multiplexer #(.select(2)) multiplexer_1 (
    .in0(d_ff_1_qn), .in1(out_10), .in2(out_8), .in3(D0), .out(multiplexer_1_out), .sel({X1, X0}));
  Multiplexer #(.select(2)) multiplexer_2 (
    .in0(d_ff_2_qn), .in1(out_7), .in2(out_9), .in3(D1), .out(multiplexer_2_out), .sel({X1, X0}));
  Multiplexer #(.select(2)) multiplexer_3 (
    .in0(d_ff_3_qn), .in1(out_8), .in2(out_10), .in3(D2), .out(multiplexer_3_out), .sel({X1, X0}));
  Multiplexer #(.select(2)) multiplexer_4 (
    .in0(d_ff_4_qn), .in1(out_9), .in2(out_7), .in3(D3), .out(multiplexer_4_out), .sel({X1, X0}));
  D_Flip_Flop d_ff_1 (.D(multiplexer_1_out), .clk(CLK), .Q(out_7), .Qn(d_ff_1_qn));  // open: preset, reset
  D_Flip_Flop d_ff_2 (.D(multiplexer_2_out), .clk(CLK), .Q(out_8), .Qn(d_ff_2_qn));  // open: preset, reset
  D_Flip_Flop d_ff_3 (.D(multiplexer_3_out), .clk(CLK), .Q(out_9), .Qn(d_ff_3_qn));  // open: preset, reset
  D_Flip_Flop d_ff_4 (.D(multiplexer_4_out), .clk(CLK), .Q(out_10), .Qn(d_ff_4_qn));  // open: preset, reset

  // Other names for the same wires on the sheet: d = out_7; q = out_10
endmodule
