// Logisim project sr_clock_toggle.circ as structural Verilog: 1 circuit, main circuit main
module main (
);

  wire button_1_out, button_2_out, button_3_out, clock_1_out, or_1_out, or_2_out, s_r_ff_1_q, s_r_ff_1_qn,
       s_r_ff_2_q, s_r_ff_2_qn;

  Clock clock_1 (.out(clock_1_out));
  Button button_1 (.out(button_1_out));
  Button button_2 (.out(button_2_out));
  S_R_Flip_Flop s_r_ff_1 (
    .S(s_r_ff_2_q), .R(s_r_ff_2_qn), .clk(clock_1_out), .Q(s_r_ff_1_q), .reset(or_1_out), .Qn(s_r_ff_1_qn),
    .preset(button_2_out));
  or or_1 (or_1_out, button_1_out, button_3_out);
  S_R_Flip_Flop s_r_ff_2 (
    .S(s_r_ff_1_q), .R(s_r_ff_1_qn), .clk(clock_1_out), .Q(s_r_ff_2_q), .reset(or_2_out), .Qn(s_r_ff_2_qn),
    .preset(button_3_out));
  or or_2 (or_2_out, button_1_out, button_2_out);
  Button button_3 (.out(button_3_out));
  LED led_1 (.in(s_r_ff_1_q));
  LED led_2 (.in(s_r_ff_2_q));
endmodule
